# Fritzing sketch receiver (saved by Fritzing 0.9.3b)
breadboards: 1

parts:
  UNO_main = Arduino Uno (Rev3)
  rf = NRF24L01+ Breakout Board
  to_PPM = Resistor [tolerance=±5% resistance=1M package=THT]
  GPS-Neo6mv2 = EM408_CON [package=em408_con]
  R1 = Resistor [tolerance=±5% resistance=4.7k package=THT]
  R2 = Resistor [tolerance=±5% resistance=10k package=THT]
  Gyro_and_stuffs = 9 Degrees of Freedom - Sensor Stick
  PIR_Sensor = LHi958 [package=to-39]
  Funduino_Water_Sensor = Soil Moisture Sensor
  DHT11 = LM34 Temperature Sensor [package="TO92 [THT]"]
  R3 = Resistor [tolerance=±5% resistance=10k package=THT]
  HC-6 = Bluetooth HC-05 Macho
  R4 = Resistor [tolerance=±5% resistance=1k package=THT]
  R5 = Resistor [tolerance=±5% resistance=2k package=THT]

nets:
  N1: UNO_main.A3, Funduino_Water_Sensor.SIG
  N2: UNO_main.A4/SDA, Gyro_and_stuffs.SCL
  N3: UNO_main.A5/SCL, Gyro_and_stuffs.SDA
  N4: UNO_main.D9_PWM, rf.CE
  N5: UNO_main.D10_PWM/SS, rf.CS
  N6: UNO_main.D11_PWM/MOSI, rf.MOSI
  N7: UNO_main.D12/MISO, rf.MISO
  N8: UNO_main.D13/SCK, rf.SCK
  GND: UNO_main.GND, rf.GND, GPS-Neo6mv2.GND, R2.Pin_0, Gyro_and_stuffs.GND, PIR_Sensor.GND, PIR_Sensor.S, Funduino_Water_Sensor.GND, DHT11.GND, HC-6.GND, R5.Pin_1
  N9: UNO_main.D0/RX, HC-6.RXD
  N10: UNO_main.D1/TX, R4.Pin_0
  N11: UNO_main.D2, to_PPM.Pin_0
  N12: UNO_main.D3_PWM, R1.Pin_0, R2.Pin_1
  N13: UNO_main.D4, GPS-Neo6mv2.RX
  N14: UNO_main.D5_PWM, PIR_Sensor.D
  N15: UNO_main.D7, DHT11.Vout, R3.Pin_1
  VCC: UNO_main.3V3, rf.VCC, GPS-Neo6mv2.VCC, Gyro_and_stuffs.VCC
  VCC_2: UNO_main.5V, Funduino_Water_Sensor.VCC, DHT11.+Vs, R3.Pin_0, HC-6.VCC
  N16: GPS-Neo6mv2.TX, R1.Pin_1
  N17: HC-6.TXD, R4.Pin_1, R5.Pin_0
