# Fritzing sketch transmitter (saved by Fritzing 0.9.3b)
breadboards: 1

parts:
  Arduino_(main) = Arduino Uno (Rev3)
  HC-05 = Bluetooth HC-05 Macho
  R1 = Resistor [tolerance=±5% resistance=1k package=THT]
  R2 = Resistor [tolerance=±5% resistance=2k package=THT]
  rf1 = NRF24L01+ Breakout Board

nets:
  N1: Arduino_(main).D9_PWM, rf1.CE
  N2: Arduino_(main).D10_PWM/SS, rf1.CS
  N3: Arduino_(main).D11_PWM/MOSI, rf1.MOSI
  N4: Arduino_(main).D12/MISO, rf1.MISO
  N5: Arduino_(main).D13/SCK, rf1.SCK
  GND: Arduino_(main).GND, HC-05.GND, R2.Pin_1, rf1.GND
  N6: Arduino_(main).D0/RX, HC-05.RXD
  N7: Arduino_(main).D1/TX, R1.Pin_0
  3V3: Arduino_(main).3V3, rf1.VCC
  5V: Arduino_(main).5V, HC-05.VCC
  N8: HC-05.TXD, R1.Pin_1, R2.Pin_0
